// Logisim project Practica03.circ as structural Verilog: 4 circuits, main circuit main
module main (
  input  in_1,
  output NOT
);

  Transistor transistor_1 (.in(1'b1), .out(NOT), .gate(in_1));
  Transistor #(.\type ("n")) transistor_2 (.in(1'b0), .out(NOT), .gate(in_1));
endmodule

module OR___V (
  input  in_1,
  input  in_2,
  output OR___V
);

  wire transistor_1_out;

  Transistor transistor_1 (.in(1'b1), .out(transistor_1_out), .gate(in_1));
  Transistor #(.\type ("n")) transistor_2 (.in(1'b0), .out(transistor_1_out), .gate(in_1));
  Transistor transistor_3 (.in(1'b1), .out(OR___V), .gate(transistor_1_out));
  Transistor #(.\type ("n")) transistor_4 (.in(in_2), .out(OR___V), .gate(transistor_1_out));
endmodule

module \Implicación___p_v_q  (
  input  p,
  input  q,
  output out_3
);

  wire transistor_1_out, transistor_3_out;

  Transistor transistor_1 (.in(1'b1), .out(transistor_1_out), .gate(p));
  Transistor #(.\type ("n")) transistor_2 (.in(1'b0), .out(transistor_1_out), .gate(p));
  Transistor transistor_3 (.in(1'b1), .out(transistor_3_out), .gate(transistor_1_out));
  Transistor #(.\type ("n")) transistor_4 (.in(1'b0), .out(transistor_3_out), .gate(transistor_1_out));
  Transistor transistor_5 (.in(1'b1), .out(out_3), .gate(transistor_3_out));
  Transistor #(.\type ("n")) transistor_6 (.in(q), .out(out_3), .gate(transistor_3_out));

  // Notes on the sheet:
  //   IMPLICACIÓN, (~p v q)
endmodule

module Comparador (
  input  A0,
  input  A1,
  input  B0,
  input  B1,
  output A___B,
  output A___B_2,
  output A___B_3
);

  wire and_1_out, and_2_out, and_3_out, and_4_out, and_5_out, and_6_out, and_7_out, and_8_out, and_9_out,
       and_10_out, not_1_out, not_2_out, not_3_out, not_4_out, not_5_out, not_6_out, not_7_out, not_8_out;

  not not_1 (not_1_out, A0);
  not not_2 (not_2_out, A1);
  not not_3 (not_3_out, A0);
  not not_4 (not_4_out, A1);
  not not_5 (not_5_out, B0);
  not not_6 (not_6_out, B1);
  not not_7 (not_7_out, B0);
  not not_8 (not_8_out, B1);
  and and_1 (and_1_out, A0, not_7_out);
  and and_2 (and_2_out, A1, not_7_out, not_8_out);
  and and_3 (and_3_out, A0, A1, not_8_out);
  and and_4 (and_4_out, not_1_out, B0);
  and and_5 (and_5_out, B0, B1, not_2_out);
  and and_6 (and_6_out, not_1_out, not_2_out, B1);
  and and_7 (and_7_out, not_3_out, not_4_out, not_5_out, not_6_out);
  and and_8 (and_8_out, not_3_out, A1, not_5_out, B1);
  and and_9 (and_9_out, A0, not_4_out, B0, not_6_out);
  and and_10 (and_10_out, A0, A1, B0, B1);
  or or_1 (A___B, and_1_out, and_2_out, and_3_out);
  or or_2 (A___B_2, and_4_out, and_5_out, and_6_out);
  or or_3 (A___B_3, and_7_out, and_8_out, and_9_out, and_10_out);
endmodule
