// Logisim project fola.circ as structural Verilog: 1 circuit, main circuit main
module main (
  input  in_1,
  input  in_2,
  input  in_3,
  input  in_4,
  input  in_5,
  input  in_6,
  output out_7,
  output out_8,
  output out_9,
  output out_10
);

  wire and_1_out, and_2_out, and_3_out, or_1_out;

  not not_1 (out_8, in_1);
  and and_1 (and_1_out, in_3, in_1);
  and and_2 (and_2_out, in_4, in_5);
  and and_3 (and_3_out, out_8, in_2);
  or or_1 (or_1_out, in_4, in_5);
  Multiplexer multiplexer_1 (.in1(or_1_out), .out(out_10), .sel(in_6));  // open: in0, en
  or or_2 (out_9, and_3_out, and_1_out);

  assign out_7 = in_1;
endmodule
