// Logisim project Practica04.circ as structural Verilog
// OR
module OR (
  input  P,
  input  Q,
  output P__Q
);

  wire transistor_1_out;

  Transistor transistor_1 (.in(1'b1), .out(transistor_1_out), .gate(P));
  Transistor #(.\type ("n")) transistor_2 (.in(1'b0), .out(transistor_1_out), .gate(P));
  Transistor transistor_3 (.in(1'b1), .out(P__Q), .gate(transistor_1_out));
  Transistor #(.\type ("n")) transistor_4 (.in(Q), .out(P__Q), .gate(transistor_1_out));

  // Notes on the sheet:
  //   OR (||)
endmodule

// NOT
module NOT (
  input  P,
  output nP
);

  Transistor transistor_1 (.in(1'b1), .out(nP), .gate(P));
  Transistor #(.\type ("n")) transistor_2 (.in(1'b0), .out(nP), .gate(P));

  // Notes on the sheet:
  //   NOT (~)
endmodule

// +
module Sumador (
  input  C_i,
  input  A,
  input  B,
  output Suma,
  output C_i_1
);

  wire AND_2_out, AND_out, XOR_out_3;

  and AND (AND_out, A, C_i);
  XOR XOR (.in_1(C_i), .in_2(A), .out_3(XOR_out_3));
  and AND_2 (AND_2_out, B, XOR_out_3);
  XOR XOR_2 (.in_1(XOR_out_3), .in_2(B), .out_3(Suma));
  OR or_1 (.P(AND_2_out), .Q(AND_out), .P__Q(C_i_1));
endmodule

module XOR (
  input  in_1,
  input  in_2,
  output out_3
);

  wire and_1_out, and_2_out, not_1_out, not_2_out;

  not not_1 (not_1_out, in_1);
  not not_2 (not_2_out, in_2);
  and and_1 (and_1_out, not_1_out, in_2);
  and and_2 (and_2_out, in_1, not_2_out);
  or or_1 (out_3, and_1_out, and_2_out);
endmodule

// ALU
module ALU__1_bit (
  input  C_i,
  input  [1:0] in_2,
  input  A,
  input  B,
  output Salida,
  output C_i_1
);

  wire AND_out, or_1_p__q, sumador_1_suma;

  and AND (AND_out, A, B);
  OR or_1 (.P(A), .Q(B), .P__Q(or_1_p__q));
  Sumador sumador_1 (.C_i(C_i), .A(A), .B(B), .Suma(sumador_1_suma), .C_i_1(C_i_1));
  Multiplexer #(.select(2)) multiplexer_1 (
    .in0(AND_out), .in1(or_1_p__q), .in2(sumador_1_suma), .out(Salida), .sel(in_2));  // open: in3, en
endmodule

module ALU__8_bits (
  input  [1:0] Operacion,
  input  [7:0] A,
  input  [7:0] B,
  output [7:0] Salida,
  output Ci__1
);

  wire alu_1_bit_1_c_i_1, alu_1_bit_2_c_i_1, alu_1_bit_3_c_i_1, alu_1_bit_4_c_i_1, alu_1_bit_5_c_i_1,
       alu_1_bit_6_c_i_1, alu_1_bit_7_c_i_1;

  ALU__1_bit alu_1_bit_1 (
    .A(A[0]), .B(B[0]), .Salida(Salida[0]), .C_i(1'b0), .in_2(Operacion), .C_i_1(alu_1_bit_1_c_i_1));
  ALU__1_bit alu_1_bit_2 (
    .A(A[1]), .B(B[1]), .Salida(Salida[1]), .C_i(alu_1_bit_1_c_i_1), .in_2(Operacion),
    .C_i_1(alu_1_bit_2_c_i_1));
  ALU__1_bit alu_1_bit_3 (
    .A(A[2]), .B(B[2]), .Salida(Salida[2]), .C_i(alu_1_bit_2_c_i_1), .in_2(Operacion),
    .C_i_1(alu_1_bit_3_c_i_1));
  ALU__1_bit alu_1_bit_4 (
    .A(A[3]), .B(B[3]), .Salida(Salida[3]), .C_i(alu_1_bit_3_c_i_1), .in_2(Operacion),
    .C_i_1(alu_1_bit_4_c_i_1));
  ALU__1_bit alu_1_bit_5 (
    .A(A[4]), .B(B[4]), .Salida(Salida[4]), .C_i(alu_1_bit_4_c_i_1), .in_2(Operacion),
    .C_i_1(alu_1_bit_5_c_i_1));
  ALU__1_bit alu_1_bit_6 (
    .A(A[5]), .B(B[5]), .Salida(Salida[5]), .C_i(alu_1_bit_5_c_i_1), .in_2(Operacion),
    .C_i_1(alu_1_bit_6_c_i_1));
  ALU__1_bit alu_1_bit_7 (
    .A(A[6]), .B(B[6]), .Salida(Salida[6]), .C_i(alu_1_bit_6_c_i_1), .in_2(Operacion),
    .C_i_1(alu_1_bit_7_c_i_1));
  ALU__1_bit alu_1_bit_8 (
    .A(A[7]), .B(B[7]), .Salida(Salida[7]), .C_i(alu_1_bit_7_c_i_1), .in_2(Operacion), .C_i_1(Ci__1));

  // Notes on the sheet:
  //   Acarreo de entrada
endmodule

module ALU__1_bit__Resta (
  input  Sumar___Restar,
  input  C_i,
  input  [1:0] AND_OR__Operar,
  input  A,
  input  B,
  output Salida,
  output C_i_1
);

  wire AND_out, multiplexer_1_out, not_1_np, or_1_p__q, Sumador_suma;

  NOT not_1 (.P(B), .nP(not_1_np));
  and AND (AND_out, A, B);
  OR or_1 (.P(A), .Q(B), .P__Q(or_1_p__q));
  Multiplexer multiplexer_1 (.in0(B), .in1(not_1_np), .out(multiplexer_1_out), .sel(Sumar___Restar));  // open: en
  Sumador Sumador (.C_i(C_i), .A(A), .B(multiplexer_1_out), .Suma(Sumador_suma), .C_i_1(C_i_1));
  Multiplexer #(.select(2)) multiplexer_2 (
    .in0(AND_out), .in1(or_1_p__q), .in2(Sumador_suma), .out(Salida), .sel(AND_OR__Operar));  // open: in3, en
endmodule

module ALU__8_bits__Igualdad (
  input  SUMAR___RESTAR___ACARREO,
  input  [1:0] Operar,
  input  [7:0] A,
  input  [7:0] B,
  output Salida,
  output Ci_1
);

  wire alu_1_bit_resta_1_c_i_1, alu_1_bit_resta_1_salida, alu_1_bit_resta_2_c_i_1, alu_1_bit_resta_2_salida,
       alu_1_bit_resta_3_c_i_1, alu_1_bit_resta_3_salida, alu_1_bit_resta_4_c_i_1, alu_1_bit_resta_4_salida,
       alu_1_bit_resta_5_c_i_1, alu_1_bit_resta_5_salida, alu_1_bit_resta_6_c_i_1, alu_1_bit_resta_6_salida,
       alu_1_bit_resta_7_c_i_1, alu_1_bit_resta_7_salida, alu_1_bit_resta_8_salida, and_1_out, COM_a___b,
       comparador_4_bits_auxiliar_1_a___b;

  ALU__1_bit__Resta alu_1_bit_resta_1 (
    .A(A[0]), .B(B[0]), .Salida(alu_1_bit_resta_1_salida), .C_i(SUMAR___RESTAR___ACARREO),
    .AND_OR__Operar(Operar), .C_i_1(alu_1_bit_resta_1_c_i_1), .Sumar___Restar(SUMAR___RESTAR___ACARREO));
  ALU__1_bit__Resta alu_1_bit_resta_2 (
    .A(A[1]), .B(B[1]), .Salida(alu_1_bit_resta_2_salida), .C_i(alu_1_bit_resta_1_c_i_1),
    .AND_OR__Operar(Operar), .C_i_1(alu_1_bit_resta_2_c_i_1), .Sumar___Restar(SUMAR___RESTAR___ACARREO));
  ALU__1_bit__Resta alu_1_bit_resta_3 (
    .A(A[2]), .B(B[2]), .Salida(alu_1_bit_resta_3_salida), .C_i(alu_1_bit_resta_2_c_i_1),
    .AND_OR__Operar(Operar), .C_i_1(alu_1_bit_resta_3_c_i_1), .Sumar___Restar(SUMAR___RESTAR___ACARREO));
  ALU__1_bit__Resta alu_1_bit_resta_4 (
    .A(A[3]), .B(B[3]), .Salida(alu_1_bit_resta_4_salida), .C_i(alu_1_bit_resta_3_c_i_1),
    .AND_OR__Operar(Operar), .C_i_1(alu_1_bit_resta_4_c_i_1), .Sumar___Restar(SUMAR___RESTAR___ACARREO));
  ALU__1_bit__Resta alu_1_bit_resta_5 (
    .A(A[4]), .B(B[4]), .Salida(alu_1_bit_resta_5_salida), .C_i(alu_1_bit_resta_4_c_i_1),
    .AND_OR__Operar(Operar), .C_i_1(alu_1_bit_resta_5_c_i_1), .Sumar___Restar(SUMAR___RESTAR___ACARREO));
  ALU__1_bit__Resta alu_1_bit_resta_6 (
    .A(A[5]), .B(B[5]), .Salida(alu_1_bit_resta_6_salida), .C_i(alu_1_bit_resta_5_c_i_1),
    .AND_OR__Operar(Operar), .C_i_1(alu_1_bit_resta_6_c_i_1), .Sumar___Restar(SUMAR___RESTAR___ACARREO));
  ALU__1_bit__Resta alu_1_bit_resta_7 (
    .A(A[6]), .B(B[6]), .Salida(alu_1_bit_resta_7_salida), .C_i(alu_1_bit_resta_6_c_i_1),
    .AND_OR__Operar(Operar), .C_i_1(alu_1_bit_resta_7_c_i_1), .Sumar___Restar(SUMAR___RESTAR___ACARREO));
  ALU__1_bit__Resta alu_1_bit_resta_8 (
    .A(A[7]), .B(B[7]), .Salida(alu_1_bit_resta_8_salida), .C_i(alu_1_bit_resta_7_c_i_1),
    .AND_OR__Operar(Operar), .C_i_1(Ci_1), .Sumar___Restar(SUMAR___RESTAR___ACARREO));
  Comparador_4_bits__Auxiliar COM (
    .in_1(alu_1_bit_resta_1_salida), .in_2(alu_1_bit_resta_2_salida), .in_3(alu_1_bit_resta_3_salida),
    .in_4(alu_1_bit_resta_4_salida), .A___B(COM_a___b));
  Comparador_4_bits__Auxiliar comparador_4_bits_auxiliar_1 (
    .in_1(alu_1_bit_resta_5_salida), .in_2(alu_1_bit_resta_6_salida), .in_3(alu_1_bit_resta_7_salida),
    .in_4(alu_1_bit_resta_8_salida), .A___B(comparador_4_bits_auxiliar_1_a___b));
  and and_1 (and_1_out, COM_a___b, comparador_4_bits_auxiliar_1_a___b);
  and and_2 (Salida, and_1_out, Ci_1);

  // Notes on the sheet:
  //   COM
endmodule

// =
module Comparador_4_bits__Auxiliar (
  input  in_1,
  input  in_2,
  input  in_3,
  input  in_4,
  output A___B
);

  wire and_1_out, and_2_out, and_3_out, and_4_out, not_1_out, not_2_out, not_3_out, not_4_out;

  not not_1 (not_1_out, in_1);
  not not_2 (not_2_out, in_2);
  not not_3 (not_3_out, in_3);
  not not_4 (not_4_out, in_4);
  and and_1 (and_1_out, not_1_out, not_2_out, not_3_out, not_4_out);
  and and_2 (and_2_out, not_1_out, in_2, not_3_out, in_4);
  and and_3 (and_3_out, in_1, not_2_out, in_3, not_4_out);
  and and_4 (and_4_out, in_1, in_2, in_3, in_4);
  or or_1 (A___B, and_1_out, and_2_out, and_3_out, and_4_out);
endmodule

module ALU___NOR (
  input  Sumar___Restar,
  input  Ci,
  input  [1:0] in_3,
  input  A,
  input  B,
  output out_6,
  output C_i_1
);

  wire AND_out, multiplexer_1_out, not_1_np, not_2_np, or_1_out, or_2_p__q, sumador_1_suma;

  NOT not_1 (.P(B), .nP(not_1_np));
  Multiplexer multiplexer_1 (.in0(B), .in1(not_1_np), .out(multiplexer_1_out), .sel(Sumar___Restar));  // open: en
  or or_1 (or_1_out, A, B);
  NOT not_2 (.P(or_1_out), .nP(not_2_np));
  and AND (AND_out, A, B);
  OR or_2 (.P(A), .Q(B), .P__Q(or_2_p__q));
  Sumador sumador_1 (.C_i(Ci), .A(A), .B(multiplexer_1_out), .Suma(sumador_1_suma), .C_i_1(C_i_1));
  Multiplexer #(.select(2)) multiplexer_2 (
    .in0(AND_out), .in1(or_2_p__q), .in2(not_2_np), .in3(sumador_1_suma), .out(out_6), .sel(in_3));  // open: en
endmodule

module ALU_final__8_bits (
  input  [1:0] Switch,
  input  Sumar_Restar,
  input  [7:0] A,
  input  [7:0] B,
  output [7:0] Salida,
  output Ci_1
);

  wire alu_nor_1_c_i_1, alu_nor_2_c_i_1, alu_nor_3_c_i_1, alu_nor_4_c_i_1, alu_nor_5_c_i_1, alu_nor_6_c_i_1,
       alu_nor_7_c_i_1;

  ALU___NOR alu_nor_1 (
    .A(A[0]), .B(B[0]), .out_6(Salida[0]), .Sumar___Restar(Sumar_Restar), .Ci(Sumar_Restar), .in_3(Switch),
    .C_i_1(alu_nor_1_c_i_1));
  ALU___NOR alu_nor_2 (
    .A(A[1]), .B(B[1]), .out_6(Salida[1]), .Sumar___Restar(Sumar_Restar), .Ci(alu_nor_1_c_i_1),
    .in_3(Switch), .C_i_1(alu_nor_2_c_i_1));
  ALU___NOR alu_nor_3 (
    .A(A[2]), .B(B[2]), .out_6(Salida[2]), .Sumar___Restar(Sumar_Restar), .Ci(alu_nor_2_c_i_1),
    .in_3(Switch), .C_i_1(alu_nor_3_c_i_1));
  ALU___NOR alu_nor_4 (
    .A(A[3]), .B(B[3]), .out_6(Salida[3]), .Sumar___Restar(Sumar_Restar), .Ci(alu_nor_3_c_i_1),
    .in_3(Switch), .C_i_1(alu_nor_4_c_i_1));
  ALU___NOR alu_nor_5 (
    .A(A[4]), .B(B[4]), .out_6(Salida[4]), .Sumar___Restar(Sumar_Restar), .Ci(alu_nor_4_c_i_1),
    .in_3(Switch), .C_i_1(alu_nor_5_c_i_1));
  ALU___NOR alu_nor_6 (
    .A(A[5]), .B(B[5]), .out_6(Salida[5]), .Sumar___Restar(Sumar_Restar), .Ci(alu_nor_5_c_i_1),
    .in_3(Switch), .C_i_1(alu_nor_6_c_i_1));
  ALU___NOR alu_nor_7 (
    .A(A[6]), .B(B[6]), .out_6(Salida[6]), .Sumar___Restar(Sumar_Restar), .Ci(alu_nor_6_c_i_1),
    .in_3(Switch), .C_i_1(alu_nor_7_c_i_1));
  ALU___NOR alu_nor_8 (
    .A(A[7]), .B(B[7]), .out_6(Salida[7]), .Sumar___Restar(Sumar_Restar), .Ci(alu_nor_7_c_i_1),
    .in_3(Switch), .C_i_1(Ci_1));
endmodule
