// Logisim project Practica05 (1).circ as structural Verilog: 9 circuits, main circuit main
// FF D
module main (
  input  Reloj,
  input  D,
  output Q
);

  D_Flip_Flop d_ff_1 (.clk(Reloj), .D(D), .Q(Q));  // open: Qn, preset, en, reset
endmodule

// Reg
module Registro_8_bits (
  input  Reloj,
  input  [7:0] Entrada_a_escribir,
  output [7:0] Registro
);

  main main_1 (.D(Entrada_a_escribir[0]), .Q(Registro[0]), .Reloj(Reloj));
  main main_2 (.D(Entrada_a_escribir[1]), .Q(Registro[1]), .Reloj(Reloj));
  main main_3 (.D(Entrada_a_escribir[2]), .Q(Registro[2]), .Reloj(Reloj));
  main main_4 (.D(Entrada_a_escribir[3]), .Q(Registro[3]), .Reloj(Reloj));
  main main_5 (.D(Entrada_a_escribir[4]), .Q(Registro[4]), .Reloj(Reloj));
  main main_6 (.D(Entrada_a_escribir[5]), .Q(Registro[5]), .Reloj(Reloj));
  main main_7 (.D(Entrada_a_escribir[6]), .Q(Registro[6]), .Reloj(Reloj));
  main main_8 (.D(Entrada_a_escribir[7]), .Q(Registro[7]), .Reloj(Reloj));
endmodule

// Banco
module Banco_de_registros (
  input  [1:0] Registro_a_escribir,
  input  Reloj,
  input  [7:0] Entrada_a_escribir,
  output [7:0] Registro__1,
  output [7:0] Registro__2,
  output [7:0] Registro__3,
  output [7:0] Registro__4
);

  wire demultiplexer_1_out0, demultiplexer_1_out1, demultiplexer_1_out2, demultiplexer_1_out3, undriven;

  Demultiplexer #(.select(2)) demultiplexer_1 (
    .out0(demultiplexer_1_out0), .out1(demultiplexer_1_out1), .out2(demultiplexer_1_out2),
    .out3(demultiplexer_1_out3), .in(Reloj), .sel(Registro_a_escribir), .en(undriven));
  Registro_8_bits registro_8_bits_1 (
    .Entrada_a_escribir(Entrada_a_escribir), .Reloj(demultiplexer_1_out0), .Registro(Registro__1));
  Registro_8_bits registro_8_bits_2 (
    .Entrada_a_escribir(Entrada_a_escribir), .Reloj(demultiplexer_1_out1), .Registro(Registro__2));
  Registro_8_bits registro_8_bits_3 (
    .Entrada_a_escribir(Entrada_a_escribir), .Reloj(demultiplexer_1_out2), .Registro(Registro__3));
  Registro_8_bits registro_8_bits_4 (
    .Entrada_a_escribir(Entrada_a_escribir), .Reloj(demultiplexer_1_out3), .Registro(Registro__4));
endmodule

module Sumador (
  input  C_i,
  input  A,
  input  B,
  output Suma,
  output C_i_1
);

  wire AND_2_out, AND_out, xor_1_out_3;

  and AND (AND_out, A, C_i);
  XOR xor_1 (.in_1(C_i), .in_2(A), .out_3(xor_1_out_3));
  buf AND_2 (AND_2_out, B);  // AND_Gate
  XOR xor_2 (.in_1(xor_1_out_3), .in_2(B), .out_3(Suma));
  XOR xor_3 (.in_1(AND_2_out), .in_2(AND_out), .out_3(C_i_1));
endmodule

module ALU__1_bit (
  input  Sumar___Restar,
  input  Ci,
  input  [1:0] in_3,
  input  A,
  input  B,
  output out_6,
  output C_i_1
);

  wire AND_out, multiplexer_1_out, not_1_out, not_2_out, or_1_out, or_2_out, Sumador_suma;

  not not_1 (not_1_out, B);
  Multiplexer multiplexer_1 (.in0(B), .in1(not_1_out), .out(multiplexer_1_out), .sel(Sumar___Restar));  // open: en
  or or_1 (or_1_out, A, B);
  not not_2 (not_2_out, or_1_out);
  and AND (AND_out, A, B);
  or or_2 (or_2_out, A, B);
  Sumador Sumador (.C_i(Ci), .A(A), .B(multiplexer_1_out), .Suma(Sumador_suma), .C_i_1(C_i_1));
  Multiplexer #(.select(2)) multiplexer_2 (
    .in0(AND_out), .in1(or_2_out), .in2(not_2_out), .in3(Sumador_suma), .out(out_6), .sel(in_3));  // open: en
endmodule

// ALU
module ALU__8_bits (
  input  [1:0] Switch,
  input  Sumar_Restar,
  input  [7:0] A,
  input  [7:0] B,
  output [7:0] Salida,
  output Ci_1
);

  wire alu_1_bit_1_c_i_1, alu_1_bit_2_c_i_1, alu_1_bit_3_c_i_1, alu_1_bit_4_c_i_1, alu_1_bit_5_c_i_1,
       alu_1_bit_6_c_i_1, alu_1_bit_7_c_i_1;

  ALU__1_bit alu_1_bit_1 (
    .A(A[0]), .B(B[0]), .Sumar___Restar(Sumar_Restar), .Ci(Sumar_Restar), .in_3(Switch),
    .C_i_1(alu_1_bit_1_c_i_1), .out_6(Salida[0]));
  ALU__1_bit alu_1_bit_2 (
    .A(A[1]), .B(B[1]), .Sumar___Restar(Sumar_Restar), .Ci(alu_1_bit_1_c_i_1), .in_3(Switch),
    .C_i_1(alu_1_bit_2_c_i_1), .out_6(Salida[1]));
  ALU__1_bit alu_1_bit_3 (
    .A(A[2]), .B(B[2]), .Sumar___Restar(Sumar_Restar), .Ci(alu_1_bit_2_c_i_1), .in_3(Switch),
    .C_i_1(alu_1_bit_3_c_i_1), .out_6(Salida[2]));
  ALU__1_bit alu_1_bit_4 (
    .A(A[3]), .B(B[3]), .Sumar___Restar(Sumar_Restar), .Ci(alu_1_bit_3_c_i_1), .in_3(Switch),
    .C_i_1(alu_1_bit_4_c_i_1), .out_6(Salida[3]));
  ALU__1_bit alu_1_bit_5 (
    .A(A[4]), .B(B[4]), .Sumar___Restar(Sumar_Restar), .Ci(alu_1_bit_4_c_i_1), .in_3(Switch),
    .C_i_1(alu_1_bit_5_c_i_1), .out_6(Salida[4]));
  ALU__1_bit alu_1_bit_6 (
    .A(A[5]), .B(B[5]), .Sumar___Restar(Sumar_Restar), .Ci(alu_1_bit_5_c_i_1), .in_3(Switch),
    .C_i_1(alu_1_bit_6_c_i_1), .out_6(Salida[5]));
  ALU__1_bit alu_1_bit_7 (
    .A(A[6]), .B(B[6]), .Sumar___Restar(Sumar_Restar), .Ci(alu_1_bit_6_c_i_1), .in_3(Switch),
    .C_i_1(alu_1_bit_7_c_i_1), .out_6(Salida[6]));
  ALU__1_bit alu_1_bit_8 (
    .A(A[7]), .B(B[7]), .Sumar___Restar(Sumar_Restar), .Ci(alu_1_bit_7_c_i_1), .in_3(Switch), .C_i_1(Ci_1),
    .out_6(Salida[7]));
endmodule

module Banco___ALU (
  input  [1:0] Registro_a_escribir,
  input  [1:0] _11_Operar,
  input  _0_Sumar__1_Restar,
  input  [7:0] Operando_1,
  input  [7:0] Operando_2,
  output [7:0] Operando_1_2,
  output [7:0] Operando_2_2,
  output [7:0] Suma,
  output [7:0] Resta
);

  wire Reloj_out;
  wire [7:0] alu_8_bits_1_salida, multiplexer_1_out;

  Clock Reloj (.out(Reloj_out));
  ALU__8_bits alu_8_bits_1 (
    .Sumar_Restar(_0_Sumar__1_Restar), .A(Operando_1), .B(Operando_2), .Switch(_11_Operar),
    .Salida(alu_8_bits_1_salida));  // open: Ci_1
  Banco_de_registros banco_de_registros_1 (
    .Reloj(Reloj_out), .Entrada_a_escribir(multiplexer_1_out), .Registro_a_escribir(Registro_a_escribir),
    .Registro__1(Operando_1_2), .Registro__2(Operando_2_2), .Registro__3(Suma), .Registro__4(Resta));
  Multiplexer #(.select(2), .width(8)) multiplexer_1 (
    .in0(Operando_1), .in1(Operando_2), .in2(alu_8_bits_1_salida), .in3(alu_8_bits_1_salida),
    .out(multiplexer_1_out), .sel(Registro_a_escribir));  // open: en
endmodule

module \Autómata  (
  input  Pin
);

  wire and_1_out, and_2_out, and_3_out, Reloj_out, s_r_ff_1_q, s_r_ff_2_q;

  Clock Reloj (.out(Reloj_out));
  S_R_Flip_Flop s_r_ff_1 (
    .S(and_1_out), .clk(Reloj_out), .R(and_2_out), .Q(s_r_ff_1_q));  // open: Qn, preset, reset, en
  S_R_Flip_Flop s_r_ff_2 (
    .S(and_3_out), .clk(Reloj_out), .R(s_r_ff_2_q), .Q(s_r_ff_2_q));  // open: Qn, preset, reset, en
  and and_1 (and_1_out, ~s_r_ff_1_q, ~Pin, s_r_ff_2_q);  // AND_Gate
  and and_2 (and_2_out, s_r_ff_1_q, s_r_ff_2_q, ~Pin);  // AND_Gate
  and and_3 (and_3_out, ~s_r_ff_2_q, ~Pin);  // AND_Gate
  LED led_1 (.in(s_r_ff_1_q));
  LED led_2 (.in(s_r_ff_2_q));

  // Notes on the sheet:
  //   00 = T
  //   01 = TE
  //   10 = NT
  //   11 = NTE
endmodule

module XOR (
  input  in_1,
  input  in_2,
  output out_3
);

  wire and_1_out, and_2_out, not_1_out, not_2_out;

  not not_1 (not_1_out, in_1);
  not not_2 (not_2_out, in_2);
  and and_1 (and_1_out, not_1_out, in_2);
  and and_2 (and_2_out, in_1, not_2_out);
  or or_1 (out_3, and_1_out, and_2_out);
endmodule
